// Logisim project ALU.circ as structural Verilog: 1 circuit, main circuit main
module main (
  input  in_1,
  input  in_2,
  input  in_3,
  input  in_4,
  input  in_5,
  input  in_6,
  input  in_7,
  input  in_8,
  input  in_9,
  output overflow__bit,
  output zero_bit,
  output negative_bit,
  output out_13,
  output out_14,
  output out_15,
  output out_16
);

  wire and_1_out, and_2_out, and_3_out, and_4_out, and_5_out, and_6_out, and_7_out, and_8_out, and_9_out,
       and_10_out, and_11_out, and_12_out, and_13_out, and_14_out, and_15_out, and_16_out, and_17_out,
       and_18_out, and_19_out, and_20_out, and_21_out, and_22_out, and_23_out, and_24_out, and_25_out,
       and_26_out, and_27_out, and_28_out, and_29_out, and_30_out, and_31_out, clock_1_out, d_ff_1_q,
       d_ff_2_q, d_ff_3_q, d_ff_4_q, d_ff_7_q, d_ff_8_q, d_ff_11_q, d_ff_12_q, not_1_out, not_2_out,
       not_3_out, not_4_out, not_5_out, not_6_out, not_7_out, not_8_out, not_9_out, not_10_out, not_11_out,
       not_12_out, not_13_out, not_14_out, not_15_out, not_16_out, not_17_out, not_18_out, or_1_out,
       or_2_out, or_3_out, or_4_out, or_5_out, or_6_out, or_7_out, or_8_out, or_9_out, or_10_out, or_11_out,
       or_12_out, or_13_out, or_14_out, xor_1_out, xor_2_out, xor_3_out, xor_4_out, xor_5_out;

  Clock clock_1 (.out(clock_1_out));
  D_Flip_Flop d_ff_1 (.D(in_1), .clk(clock_1_out), .Q(d_ff_1_q));  // open: Qn, preset, reset
  D_Flip_Flop d_ff_2 (.D(in_2), .clk(clock_1_out), .Q(d_ff_2_q));  // open: Qn, preset, reset
  and and_1 (and_1_out, or_4_out, or_5_out);
  D_Flip_Flop d_ff_3 (.D(in_3), .clk(clock_1_out), .Q(d_ff_3_q));  // open: Qn, preset, reset
  and and_2 (and_2_out, or_4_out, d_ff_1_q);
  or or_1 (or_1_out, and_1_out, and_2_out, and_3_out);
  and and_3 (and_3_out, or_5_out, d_ff_1_q);
  not not_1 (not_1_out, or_1_out);
  D_Flip_Flop d_ff_4 (.D(in_4), .clk(clock_1_out), .Q(d_ff_4_q));  // open: Qn, preset, reset
  or or_2 (or_2_out, or_4_out, or_5_out, d_ff_1_q);
  and and_4 (and_4_out, not_1_out, or_2_out);
  or or_3 (or_3_out, and_4_out, and_5_out);
  and and_5 (and_5_out, or_4_out, or_5_out, d_ff_1_q);
  and and_6 (and_6_out, or_9_out, or_8_out);
  and and_7 (and_7_out, or_9_out, d_ff_2_q);
  or or_4 (or_4_out, and_6_out, and_7_out, and_8_out);
  D_Flip_Flop d_ff_5 (.D(or_3_out), .clk(clock_1_out), .Q(out_13));  // open: Qn, preset, reset
  not not_2 (not_2_out, d_ff_7_q);
  and and_8 (and_8_out, or_8_out, d_ff_2_q);
  xor xor_1 (xor_1_out, not_2_out, and_11_out);
  not not_3 (not_3_out, in_9);
  and and_9 (and_9_out, d_ff_7_q, not_3_out);
  or or_5 (or_5_out, and_9_out, and_12_out);
  or or_6 (or_6_out, or_9_out, or_8_out, d_ff_2_q);
  not not_4 (not_4_out, or_4_out);
  and and_10 (and_10_out, not_4_out, or_6_out);
  or or_7 (or_7_out, and_10_out, and_13_out);
  D_Flip_Flop d_ff_6 (.D(or_7_out), .clk(clock_1_out), .Q(out_14));  // open: Qn, preset, reset
  D_Flip_Flop d_ff_7 (.D(in_5), .clk(clock_1_out), .Q(d_ff_7_q));  // open: Qn, preset, reset
  and and_11 (and_11_out, not_5_out, and_18_out);
  and and_12 (and_12_out, xor_1_out, in_9);
  and and_13 (and_13_out, or_9_out, or_8_out, d_ff_2_q);
  D_Flip_Flop d_ff_8 (.D(in_6), .clk(clock_1_out), .Q(d_ff_8_q));  // open: Qn, preset, reset
  not not_5 (not_5_out, d_ff_8_q);
  xor xor_2 (xor_2_out, not_5_out, and_18_out);
  not not_6 (not_6_out, in_9);
  and and_14 (and_14_out, d_ff_8_q, not_6_out);
  or or_8 (or_8_out, and_14_out, and_16_out);
  and and_15 (and_15_out, and_27_out, or_10_out);
  D_Flip_Flop d_ff_9 (.D(or_13_out), .clk(clock_1_out), .Q(out_15));  // open: Qn, preset, reset
  and and_16 (and_16_out, xor_2_out, in_9);
  and and_17 (and_17_out, and_27_out, d_ff_3_q);
  or or_9 (or_9_out, and_15_out, and_17_out, and_20_out);
  D_Flip_Flop d_ff_10 (.D(xor_5_out), .clk(clock_1_out), .Q(out_16));  // open: Qn, preset, reset
  D_Flip_Flop d_ff_11 (.D(in_7), .clk(clock_1_out), .Q(d_ff_11_q));  // open: Qn, preset, reset
  not not_7 (not_7_out, d_ff_11_q);
  and and_18 (and_18_out, not_7_out, and_25_out);
  not not_8 (not_8_out, in_9);
  and and_19 (and_19_out, d_ff_11_q, not_8_out);
  or or_10 (or_10_out, and_19_out, and_21_out);
  and and_20 (and_20_out, or_10_out, d_ff_3_q);
  D_Flip_Flop d_ff_12 (.D(in_8), .clk(clock_1_out), .Q(d_ff_12_q));  // open: Qn, preset, reset
  and and_21 (and_21_out, xor_3_out, in_9);
  or or_11 (or_11_out, and_27_out, or_10_out, d_ff_3_q);
  not not_9 (not_9_out, or_9_out);
  and and_22 (and_22_out, not_9_out, or_11_out);
  xor xor_3 (xor_3_out, not_7_out, and_25_out);
  not not_10 (not_10_out, in_9);
  and and_23 (and_23_out, d_ff_12_q, not_10_out);
  or or_12 (or_12_out, and_23_out, and_26_out);
  and and_24 (and_24_out, and_27_out, or_10_out, d_ff_3_q);
  or or_13 (or_13_out, and_22_out, and_24_out);
  and and_25 (and_25_out, not_11_out, in_9);
  and and_26 (and_26_out, xor_4_out, in_9);
  not not_11 (not_11_out, d_ff_12_q);
  xor xor_4 (xor_4_out, not_11_out, in_9);
  and and_27 (and_27_out, d_ff_4_q, or_12_out);
  xor xor_5 (xor_5_out, d_ff_4_q, or_12_out);
  not not_12 (not_12_out, or_4_out);
  not not_13 (not_13_out, xor_5_out);
  not not_14 (not_14_out, or_13_out);
  not not_15 (not_15_out, or_7_out);
  not not_16 (not_16_out, or_3_out);
  not not_17 (not_17_out, or_5_out);
  not not_18 (not_18_out, d_ff_1_q);
  and and_28 (and_28_out, not_12_out, or_1_out);
  and and_29 (and_29_out, not_13_out, not_14_out, not_15_out, not_16_out);
  and and_30 (and_30_out, not_17_out, not_18_out, or_4_out);
  and and_31 (and_31_out, or_5_out, d_ff_1_q, and_28_out);
  or or_14 (or_14_out, and_30_out, and_31_out);
  D_Flip_Flop d_ff_13 (.D(or_14_out), .clk(clock_1_out), .Q(overflow__bit));  // open: Qn, preset, reset
  D_Flip_Flop d_ff_14 (.D(and_29_out), .clk(clock_1_out), .Q(zero_bit));  // open: Qn, preset, reset
  D_Flip_Flop d_ff_15 (.D(or_3_out), .clk(clock_1_out), .Q(negative_bit));  // open: Qn, preset, reset

  // Notes on the sheet:
  //   Diana Covaci
  //   261 086 280
  //   add/sub command pin
  //   left register
  //   output
  //   right register
  //   2s complement one
  //   2's complement circuit
  //   adder circuit
  //   status register
endmodule
