// Logisim project RAM.circ as structural Verilog: 1 circuit, main circuit main
module main (
  input  in_1,
  input  in_2,
  input  in_3,
  input  in_4,
  input  mode,
  input  in_6,
  input  address,
  input  in_8,
  input  in_9,
  input  in_10,
  input  in_11,
  input  in_12,
  output out_13,
  output out_14,
  output out_15,
  output out_16
);

  wire and_1_out, and_2_out, and_3_out, and_4_out, and_5_out, and_6_out, and_7_out, and_8_out, and_9_out,
       and_10_out, and_11_out, and_12_out, and_13_out, and_14_out, and_15_out, and_16_out, and_17_out,
       and_18_out, and_19_out, and_20_out, and_21_out, and_22_out, and_23_out, and_24_out, and_25_out,
       and_26_out, and_27_out, and_28_out, and_29_out, and_30_out, and_31_out, and_32_out, and_33_out,
       and_34_out, and_35_out, and_36_out, and_37_out, and_38_out, and_39_out, and_40_out, and_41_out,
       and_42_out, and_43_out, and_44_out, and_45_out, and_46_out, and_47_out, and_48_out, and_49_out,
       and_50_out, and_51_out, and_52_out, and_53_out, and_54_out, and_55_out, and_56_out, and_57_out,
       and_58_out, and_59_out, and_60_out, and_61_out, and_62_out, and_63_out, and_64_out, and_65_out,
       and_66_out, and_67_out, and_68_out, and_69_out, and_70_out, and_71_out, and_72_out, and_73_out,
       and_74_out, and_75_out, and_76_out, and_77_out, and_78_out, and_79_out, and_80_out, and_81_out,
       and_82_out, and_83_out, and_84_out, and_85_out, and_86_out, and_87_out, and_88_out, and_89_out,
       and_90_out, and_91_out, and_92_out, and_93_out, and_94_out, and_95_out, and_96_out, and_97_out,
       and_98_out, and_99_out, and_100_out, and_101_out, and_102_out, and_103_out, and_104_out, and_105_out,
       and_106_out, and_107_out, and_108_out, and_109_out, and_110_out, and_111_out, and_112_out,
       and_113_out, and_114_out, and_115_out, and_116_out, and_117_out, and_118_out, and_119_out,
       and_120_out, and_121_out, and_122_out, and_123_out, and_124_out, and_125_out, and_126_out,
       and_127_out, and_128_out, clock_1_out, d_ff_1_q, d_ff_2_q, d_ff_3_q, d_ff_4_q, d_ff_5_q, d_ff_6_q,
       d_ff_7_q, d_ff_8_q, d_ff_9_q, d_ff_10_q, d_ff_11_q, d_ff_12_q, d_ff_13_q, d_ff_14_q, d_ff_15_q,
       d_ff_16_q, d_ff_17_q, d_ff_18_q, d_ff_20_q, d_ff_21_q, d_ff_22_q, d_ff_23_q, d_ff_24_q, d_ff_25_q,
       d_ff_27_q, d_ff_28_q, d_ff_29_q, d_ff_30_q, d_ff_31_q, d_ff_32_q, d_ff_33_q, d_ff_34_q, d_ff_36_q,
       d_ff_37_q, d_ff_38_q, d_ff_39_q, d_ff_40_q, d_ff_41_q, d_ff_42_q, d_ff_43_q, not_1_out, not_2_out,
       not_3_out, not_4_out, not_5_out, not_6_out, not_7_out, not_8_out, not_9_out, not_10_out, not_11_out,
       not_12_out, not_13_out, not_14_out, not_15_out, not_16_out, not_17_out, not_18_out, not_19_out,
       not_20_out, not_21_out, not_22_out, not_23_out, not_24_out, not_25_out, not_26_out, not_27_out,
       not_28_out, not_29_out, not_30_out, not_31_out, not_32_out, not_33_out, not_34_out, not_35_out,
       not_36_out, not_37_out, not_38_out, not_39_out, not_40_out, not_41_out, not_42_out, not_43_out,
       not_44_out, not_45_out, not_46_out, not_47_out, not_48_out, not_49_out, not_50_out, not_51_out,
       not_52_out, not_53_out, not_54_out, not_55_out, not_56_out, or_1_out, or_2_out, or_3_out, or_4_out,
       or_5_out, or_6_out, or_7_out, or_8_out, or_9_out, or_10_out, or_11_out, or_12_out, or_13_out,
       or_14_out, or_15_out, or_16_out, or_17_out, or_18_out, or_19_out, or_20_out, or_21_out, or_22_out,
       or_23_out, or_24_out, or_25_out, or_26_out, or_27_out, or_28_out, or_29_out, or_30_out, or_31_out,
       or_32_out, or_33_out, or_34_out, or_35_out, or_36_out, or_37_out, or_38_out, or_39_out, or_40_out,
       or_41_out, or_42_out, or_43_out, or_44_out, or_45_out, or_46_out, or_47_out, or_48_out, or_49_out,
       or_50_out, or_51_out, or_52_out, or_53_out, or_54_out, or_55_out, or_56_out, or_57_out, or_58_out,
       or_59_out, or_60_out, or_61_out, or_62_out, or_63_out, or_64_out, or_65_out, or_66_out, or_67_out,
       or_68_out;

  Clock clock_1 (.out(clock_1_out));
  D_Flip_Flop d_ff_1 (.D(mode), .clk(clock_1_out), .Q(d_ff_1_q));  // open: Qn, preset, reset
  D_Flip_Flop d_ff_2 (.D(in_6), .clk(clock_1_out), .Q(d_ff_2_q));  // open: Qn, preset, reset
  D_Flip_Flop d_ff_3 (.D(address), .clk(clock_1_out), .Q(d_ff_3_q));  // open: Qn, preset, reset
  D_Flip_Flop d_ff_4 (.D(in_8), .clk(clock_1_out), .Q(d_ff_4_q));  // open: Qn, preset, reset
  and and_1 (and_1_out, d_ff_2_q, d_ff_3_q, clock_1_out, d_ff_4_q);
  not not_1 (not_1_out, d_ff_4_q);
  not not_2 (not_2_out, d_ff_3_q);
  not not_3 (not_3_out, d_ff_3_q);
  not not_4 (not_4_out, d_ff_4_q);
  not not_5 (not_5_out, d_ff_2_q);
  not not_6 (not_6_out, d_ff_2_q);
  not not_7 (not_7_out, d_ff_4_q);
  not not_8 (not_8_out, d_ff_2_q);
  not not_9 (not_9_out, d_ff_3_q);
  not not_10 (not_10_out, d_ff_2_q);
  not not_11 (not_11_out, d_ff_3_q);
  not not_12 (not_12_out, d_ff_4_q);
  and and_2 (and_2_out, d_ff_2_q, d_ff_3_q, clock_1_out, not_1_out);
  and and_3 (and_3_out, d_ff_2_q, not_2_out, clock_1_out, d_ff_4_q);
  and and_4 (and_4_out, d_ff_2_q, not_3_out, clock_1_out, not_4_out);
  and and_5 (and_5_out, not_5_out, d_ff_3_q, clock_1_out, d_ff_4_q);
  and and_6 (and_6_out, not_6_out, d_ff_3_q, clock_1_out, not_7_out);
  and and_7 (and_7_out, not_8_out, not_9_out, clock_1_out, d_ff_4_q);
  and and_8 (and_8_out, not_10_out, not_11_out, clock_1_out, not_12_out);
  D_Flip_Flop d_ff_5 (.D(in_9), .clk(clock_1_out), .Q(d_ff_5_q));  // open: Qn, preset, reset
  D_Flip_Flop d_ff_6 (.D(in_10), .clk(clock_1_out), .Q(d_ff_6_q));  // open: Qn, preset, reset
  D_Flip_Flop d_ff_7 (.D(in_11), .clk(clock_1_out), .Q(d_ff_7_q));  // open: Qn, preset, reset
  and and_9 (and_9_out, and_1_out, not_14_out);
  and and_10 (and_10_out, and_2_out, d_ff_1_q);
  and and_11 (and_11_out, and_2_out, not_16_out);
  and and_12 (and_12_out, and_3_out, d_ff_1_q);
  and and_13 (and_13_out, and_3_out, not_18_out);
  and and_14 (and_14_out, d_ff_1_q, and_4_out);
  and and_15 (and_15_out, and_4_out, not_20_out);
  and and_16 (and_16_out, and_5_out, not_22_out);
  and and_17 (and_17_out, and_6_out, not_24_out);
  and and_18 (and_18_out, and_7_out, not_26_out);
  and and_19 (and_19_out, and_8_out, not_28_out);
  and and_20 (and_20_out, and_1_out, d_ff_1_q);
  or or_1 (or_1_out, and_22_out, and_21_out);
  and and_21 (and_21_out, not_13_out, d_ff_11_q);
  and and_22 (and_22_out, and_9_out, d_ff_5_q);
  not not_13 (not_13_out, and_9_out);
  not not_14 (not_14_out, d_ff_1_q);
  D_Flip_Flop #(.trigger("falling")) d_ff_8 (.D(or_2_out), .clk(clock_1_out), .Q(d_ff_8_q));  // open: Qn, preset, reset
  or or_2 (or_2_out, and_23_out, and_24_out);
  and and_23 (and_23_out, and_11_out, d_ff_5_q);
  and and_24 (and_24_out, not_15_out, d_ff_8_q);
  not not_15 (not_15_out, and_11_out);
  not not_16 (not_16_out, d_ff_1_q);
  D_Flip_Flop #(.trigger("falling")) d_ff_9 (.D(or_3_out), .clk(clock_1_out), .Q(d_ff_9_q));  // open: Qn, preset, reset
  or or_3 (or_3_out, and_26_out, and_25_out);
  and and_25 (and_25_out, not_17_out, d_ff_9_q);
  and and_26 (and_26_out, and_13_out, d_ff_5_q);
  not not_17 (not_17_out, and_13_out);
  not not_18 (not_18_out, d_ff_1_q);
  or or_4 (or_4_out, and_27_out, and_28_out);
  and and_27 (and_27_out, and_15_out, d_ff_5_q);
  and and_28 (and_28_out, not_19_out, d_ff_12_q);
  not not_19 (not_19_out, and_15_out);
  not not_20 (not_20_out, d_ff_1_q);
  and and_29 (and_29_out, d_ff_1_q, and_5_out);
  or or_5 (or_5_out, and_31_out, and_30_out);
  and and_30 (and_30_out, not_21_out, d_ff_13_q);
  and and_31 (and_31_out, and_16_out, d_ff_5_q);
  not not_21 (not_21_out, and_16_out);
  not not_22 (not_22_out, d_ff_1_q);
  and and_32 (and_32_out, d_ff_1_q, and_6_out);
  or or_6 (or_6_out, and_33_out, and_34_out);
  and and_33 (and_33_out, and_17_out, d_ff_5_q);
  and and_34 (and_34_out, not_23_out, d_ff_14_q);
  not not_23 (not_23_out, and_17_out);
  not not_24 (not_24_out, d_ff_1_q);
  and and_35 (and_35_out, d_ff_1_q, and_7_out);
  or or_7 (or_7_out, and_36_out, and_37_out);
  and and_36 (and_36_out, and_18_out, d_ff_5_q);
  and and_37 (and_37_out, not_25_out, d_ff_15_q);
  not not_25 (not_25_out, and_18_out);
  not not_26 (not_26_out, d_ff_1_q);
  and and_38 (and_38_out, d_ff_1_q, and_8_out);
  or or_8 (or_8_out, and_40_out, and_39_out);
  and and_39 (and_39_out, not_27_out, d_ff_16_q);
  and and_40 (and_40_out, and_19_out, d_ff_5_q);
  not not_27 (not_27_out, and_19_out);
  not not_28 (not_28_out, d_ff_1_q);
  D_Flip_Flop d_ff_10 (.D(in_12), .clk(clock_1_out), .Q(d_ff_10_q));  // open: Qn, preset, reset
  D_Flip_Flop #(.trigger("falling")) d_ff_11 (
    .D(or_1_out), .clk(clock_1_out), .Q(d_ff_11_q));  // open: Qn, preset, reset
  D_Flip_Flop #(.trigger("falling")) d_ff_12 (
    .D(or_4_out), .clk(clock_1_out), .Q(d_ff_12_q));  // open: Qn, preset, reset
  D_Flip_Flop #(.trigger("falling")) d_ff_13 (
    .D(or_5_out), .clk(clock_1_out), .Q(d_ff_13_q));  // open: Qn, preset, reset
  D_Flip_Flop #(.trigger("falling")) d_ff_14 (
    .D(or_6_out), .clk(clock_1_out), .Q(d_ff_14_q));  // open: Qn, preset, reset
  D_Flip_Flop #(.trigger("falling")) d_ff_15 (
    .D(or_7_out), .clk(clock_1_out), .Q(d_ff_15_q));  // open: Qn, preset, reset
  D_Flip_Flop #(.trigger("falling")) d_ff_16 (
    .D(or_8_out), .clk(clock_1_out), .Q(d_ff_16_q));  // open: Qn, preset, reset
  and and_41 (and_41_out, and_20_out, d_ff_11_q);
  and and_42 (and_42_out, and_10_out, d_ff_8_q);
  and and_43 (and_43_out, and_12_out, d_ff_9_q);
  and and_44 (and_44_out, and_14_out, d_ff_12_q);
  and and_45 (and_45_out, and_29_out, d_ff_13_q);
  and and_46 (and_46_out, and_32_out, d_ff_14_q);
  and and_47 (and_47_out, and_35_out, d_ff_15_q);
  and and_48 (and_48_out, and_38_out, d_ff_16_q);
  or or_9 (or_9_out, and_49_out, and_66_out);
  and and_49 (and_49_out, d_ff_1_q, or_39_out);
  or or_10 (or_10_out, and_51_out, and_50_out);
  and and_50 (and_50_out, not_29_out, d_ff_20_q);
  and and_51 (and_51_out, and_9_out, d_ff_6_q);
  not not_29 (not_29_out, and_9_out);
  D_Flip_Flop #(.trigger("falling")) d_ff_17 (
    .D(or_11_out), .clk(clock_1_out), .Q(d_ff_17_q));  // open: Qn, preset, reset
  or or_11 (or_11_out, and_53_out, and_52_out);
  and and_52 (and_52_out, not_30_out, d_ff_17_q);
  and and_53 (and_53_out, and_11_out, d_ff_6_q);
  not not_30 (not_30_out, and_11_out);
  D_Flip_Flop #(.trigger("falling")) d_ff_18 (
    .D(or_12_out), .clk(clock_1_out), .Q(d_ff_18_q));  // open: Qn, preset, reset
  or or_12 (or_12_out, and_55_out, and_54_out);
  and and_54 (and_54_out, not_31_out, d_ff_18_q);
  and and_55 (and_55_out, and_13_out, d_ff_6_q);
  not not_31 (not_31_out, and_13_out);
  or or_13 (or_13_out, and_56_out, and_57_out);
  and and_56 (and_56_out, and_15_out, d_ff_6_q);
  and and_57 (and_57_out, not_32_out, d_ff_21_q);
  not not_32 (not_32_out, and_15_out);
  or or_14 (or_14_out, and_59_out, and_58_out);
  and and_58 (and_58_out, not_33_out, d_ff_22_q);
  and and_59 (and_59_out, and_16_out, d_ff_6_q);
  not not_33 (not_33_out, and_16_out);
  or or_15 (or_15_out, and_61_out, and_60_out);
  and and_60 (and_60_out, not_34_out, d_ff_23_q);
  and and_61 (and_61_out, and_17_out, d_ff_6_q);
  not not_34 (not_34_out, and_17_out);
  or or_16 (or_16_out, and_62_out, and_63_out);
  and and_62 (and_62_out, and_18_out, d_ff_6_q);
  and and_63 (and_63_out, not_35_out, d_ff_24_q);
  not not_35 (not_35_out, and_18_out);
  or or_17 (or_17_out, and_64_out, and_65_out);
  and and_64 (and_64_out, and_19_out, d_ff_6_q);
  and and_65 (and_65_out, not_36_out, d_ff_25_q);
  not not_36 (not_36_out, and_19_out);
  D_Flip_Flop #(.trigger("falling")) d_ff_19 (.D(or_9_out), .clk(clock_1_out), .Q(out_13));  // open: Qn, preset, reset
  and and_66 (and_66_out, not_37_out, out_13);
  not not_37 (not_37_out, d_ff_1_q);
  D_Flip_Flop #(.trigger("falling")) d_ff_20 (
    .D(or_10_out), .clk(clock_1_out), .Q(d_ff_20_q));  // open: Qn, preset, reset
  D_Flip_Flop #(.trigger("falling")) d_ff_21 (
    .D(or_13_out), .clk(clock_1_out), .Q(d_ff_21_q));  // open: Qn, preset, reset
  D_Flip_Flop #(.trigger("falling")) d_ff_22 (
    .D(or_14_out), .clk(clock_1_out), .Q(d_ff_22_q));  // open: Qn, preset, reset
  D_Flip_Flop #(.trigger("falling")) d_ff_23 (
    .D(or_15_out), .clk(clock_1_out), .Q(d_ff_23_q));  // open: Qn, preset, reset
  D_Flip_Flop #(.trigger("falling")) d_ff_24 (
    .D(or_16_out), .clk(clock_1_out), .Q(d_ff_24_q));  // open: Qn, preset, reset
  D_Flip_Flop #(.trigger("falling")) d_ff_25 (
    .D(or_17_out), .clk(clock_1_out), .Q(d_ff_25_q));  // open: Qn, preset, reset
  and and_67 (and_67_out, and_20_out, d_ff_20_q);
  and and_68 (and_68_out, and_10_out, d_ff_17_q);
  and and_69 (and_69_out, and_12_out, d_ff_18_q);
  and and_70 (and_70_out, and_14_out, d_ff_21_q);
  and and_71 (and_71_out, and_29_out, d_ff_22_q);
  and and_72 (and_72_out, and_32_out, d_ff_23_q);
  and and_73 (and_73_out, and_35_out, d_ff_24_q);
  and and_74 (and_74_out, and_38_out, d_ff_25_q);
  or or_18 (or_18_out, and_75_out, and_86_out);
  and and_75 (and_75_out, d_ff_1_q, or_38_out);
  or or_19 (or_19_out, and_76_out, and_87_out);
  and and_76 (and_76_out, and_9_out, d_ff_7_q);
  not not_38 (not_38_out, and_9_out);
  or or_20 (or_20_out, and_77_out, and_78_out);
  and and_77 (and_77_out, and_11_out, d_ff_7_q);
  and and_78 (and_78_out, not_39_out, d_ff_28_q);
  not not_39 (not_39_out, and_11_out);
  or or_21 (or_21_out, and_80_out, and_79_out);
  and and_79 (and_79_out, not_40_out, d_ff_29_q);
  and and_80 (and_80_out, and_13_out, d_ff_7_q);
  not not_40 (not_40_out, and_13_out);
  or or_22 (or_22_out, and_81_out, and_88_out);
  and and_81 (and_81_out, and_15_out, d_ff_7_q);
  not not_41 (not_41_out, and_15_out);
  or or_23 (or_23_out, and_82_out, and_89_out);
  and and_82 (and_82_out, and_16_out, d_ff_7_q);
  not not_42 (not_42_out, and_16_out);
  or or_24 (or_24_out, and_83_out, and_90_out);
  and and_83 (and_83_out, and_17_out, d_ff_7_q);
  not not_43 (not_43_out, and_17_out);
  or or_25 (or_25_out, and_84_out, and_91_out);
  and and_84 (and_84_out, and_18_out, d_ff_7_q);
  not not_44 (not_44_out, and_18_out);
  or or_26 (or_26_out, and_85_out, and_92_out);
  and and_85 (and_85_out, and_19_out, d_ff_7_q);
  not not_45 (not_45_out, and_19_out);
  D_Flip_Flop #(.trigger("falling")) d_ff_26 (.D(or_18_out), .clk(clock_1_out), .Q(out_14));  // open: Qn, preset, reset
  and and_86 (and_86_out, not_46_out, out_14);
  not not_46 (not_46_out, d_ff_1_q);
  D_Flip_Flop #(.trigger("falling")) d_ff_27 (
    .D(or_19_out), .clk(clock_1_out), .Q(d_ff_27_q));  // open: Qn, preset, reset
  and and_87 (and_87_out, not_38_out, d_ff_27_q);
  D_Flip_Flop #(.trigger("falling")) d_ff_28 (
    .D(or_20_out), .clk(clock_1_out), .Q(d_ff_28_q));  // open: Qn, preset, reset
  D_Flip_Flop #(.trigger("falling")) d_ff_29 (
    .D(or_21_out), .clk(clock_1_out), .Q(d_ff_29_q));  // open: Qn, preset, reset
  D_Flip_Flop #(.trigger("falling")) d_ff_30 (
    .D(or_22_out), .clk(clock_1_out), .Q(d_ff_30_q));  // open: Qn, preset, reset
  and and_88 (and_88_out, not_41_out, d_ff_30_q);
  D_Flip_Flop #(.trigger("falling")) d_ff_31 (
    .D(or_23_out), .clk(clock_1_out), .Q(d_ff_31_q));  // open: Qn, preset, reset
  and and_89 (and_89_out, not_42_out, d_ff_31_q);
  D_Flip_Flop #(.trigger("falling")) d_ff_32 (
    .D(or_24_out), .clk(clock_1_out), .Q(d_ff_32_q));  // open: Qn, preset, reset
  and and_90 (and_90_out, not_43_out, d_ff_32_q);
  D_Flip_Flop #(.trigger("falling")) d_ff_33 (
    .D(or_25_out), .clk(clock_1_out), .Q(d_ff_33_q));  // open: Qn, preset, reset
  and and_91 (and_91_out, not_44_out, d_ff_33_q);
  D_Flip_Flop #(.trigger("falling")) d_ff_34 (
    .D(or_26_out), .clk(clock_1_out), .Q(d_ff_34_q));  // open: Qn, preset, reset
  and and_92 (and_92_out, not_45_out, d_ff_34_q);
  and and_93 (and_93_out, and_20_out, d_ff_27_q);
  and and_94 (and_94_out, and_10_out, d_ff_28_q);
  and and_95 (and_95_out, and_12_out, d_ff_29_q);
  and and_96 (and_96_out, and_14_out, d_ff_30_q);
  and and_97 (and_97_out, and_29_out, d_ff_31_q);
  and and_98 (and_98_out, and_32_out, d_ff_32_q);
  and and_99 (and_99_out, and_35_out, d_ff_33_q);
  and and_100 (and_100_out, and_38_out, d_ff_34_q);
  and and_101 (and_101_out, d_ff_1_q, or_53_out);
  or or_27 (or_27_out, and_102_out, and_113_out);
  and and_102 (and_102_out, and_9_out, d_ff_10_q);
  not not_47 (not_47_out, and_9_out);
  or or_28 (or_28_out, and_104_out, and_103_out);
  and and_103 (and_103_out, not_48_out, d_ff_37_q);
  and and_104 (and_104_out, and_11_out, d_ff_10_q);
  not not_48 (not_48_out, and_11_out);
  or or_29 (or_29_out, and_106_out, and_105_out);
  and and_105 (and_105_out, not_49_out, d_ff_38_q);
  and and_106 (and_106_out, and_13_out, d_ff_10_q);
  not not_49 (not_49_out, and_13_out);
  or or_30 (or_30_out, and_107_out, and_114_out);
  and and_107 (and_107_out, and_15_out, d_ff_10_q);
  not not_50 (not_50_out, and_15_out);
  or or_31 (or_31_out, and_108_out, and_115_out);
  and and_108 (and_108_out, and_16_out, d_ff_10_q);
  not not_51 (not_51_out, and_16_out);
  or or_32 (or_32_out, and_109_out, and_116_out);
  and and_109 (and_109_out, and_17_out, d_ff_10_q);
  not not_52 (not_52_out, and_17_out);
  or or_33 (or_33_out, and_110_out, and_117_out);
  and and_110 (and_110_out, and_18_out, d_ff_10_q);
  not not_53 (not_53_out, and_18_out);
  or or_34 (or_34_out, and_111_out, and_118_out);
  and and_111 (and_111_out, and_19_out, d_ff_10_q);
  not not_54 (not_54_out, and_19_out);
  D_Flip_Flop #(.trigger("falling")) d_ff_35 (.D(or_35_out), .clk(clock_1_out), .Q(out_15));  // open: Qn, preset, reset
  or or_35 (or_35_out, and_101_out, and_112_out);
  and and_112 (and_112_out, not_55_out, out_15);
  not not_55 (not_55_out, d_ff_1_q);
  D_Flip_Flop #(.trigger("falling")) d_ff_36 (
    .D(or_27_out), .clk(clock_1_out), .Q(d_ff_36_q));  // open: Qn, preset, reset
  and and_113 (and_113_out, not_47_out, d_ff_36_q);
  D_Flip_Flop #(.trigger("falling")) d_ff_37 (
    .D(or_28_out), .clk(clock_1_out), .Q(d_ff_37_q));  // open: Qn, preset, reset
  D_Flip_Flop #(.trigger("falling")) d_ff_38 (
    .D(or_29_out), .clk(clock_1_out), .Q(d_ff_38_q));  // open: Qn, preset, reset
  D_Flip_Flop #(.trigger("falling")) d_ff_39 (
    .D(or_30_out), .clk(clock_1_out), .Q(d_ff_39_q));  // open: Qn, preset, reset
  and and_114 (and_114_out, not_50_out, d_ff_39_q);
  D_Flip_Flop #(.trigger("falling")) d_ff_40 (
    .D(or_31_out), .clk(clock_1_out), .Q(d_ff_40_q));  // open: Qn, preset, reset
  and and_115 (and_115_out, not_51_out, d_ff_40_q);
  D_Flip_Flop #(.trigger("falling")) d_ff_41 (
    .D(or_32_out), .clk(clock_1_out), .Q(d_ff_41_q));  // open: Qn, preset, reset
  and and_116 (and_116_out, not_52_out, d_ff_41_q);
  D_Flip_Flop #(.trigger("falling")) d_ff_42 (
    .D(or_33_out), .clk(clock_1_out), .Q(d_ff_42_q));  // open: Qn, preset, reset
  and and_117 (and_117_out, not_53_out, d_ff_42_q);
  D_Flip_Flop #(.trigger("falling")) d_ff_43 (
    .D(or_34_out), .clk(clock_1_out), .Q(d_ff_43_q));  // open: Qn, preset, reset
  and and_118 (and_118_out, not_54_out, d_ff_43_q);
  and and_119 (and_119_out, and_20_out, d_ff_36_q);
  and and_120 (and_120_out, and_10_out, d_ff_37_q);
  or or_36 (or_36_out, and_42_out, or_37_out);
  and and_121 (and_121_out, and_12_out, d_ff_38_q);
  or or_37 (or_37_out, and_43_out, or_43_out);
  and and_122 (and_122_out, and_14_out, d_ff_39_q);
  and and_123 (and_123_out, and_29_out, d_ff_40_q);
  and and_124 (and_124_out, and_32_out, d_ff_41_q);
  and and_125 (and_125_out, and_35_out, d_ff_42_q);
  and and_126 (and_126_out, and_38_out, d_ff_43_q);
  and and_127 (and_127_out, d_ff_1_q, or_61_out);
  or or_38 (or_38_out, and_67_out, or_40_out);
  or or_39 (or_39_out, and_41_out, or_36_out);
  or or_40 (or_40_out, and_68_out, or_41_out);
  or or_41 (or_41_out, and_69_out, or_42_out);
  or or_42 (or_42_out, and_70_out, or_44_out);
  or or_43 (or_43_out, and_44_out, or_45_out);
  or or_44 (or_44_out, and_71_out, or_46_out);
  or or_45 (or_45_out, and_45_out, or_47_out);
  or or_46 (or_46_out, and_72_out, or_48_out);
  or or_47 (or_47_out, and_46_out, or_49_out);
  or or_48 (or_48_out, and_73_out, or_50_out);
  or or_49 (or_49_out, and_47_out, or_51_out);
  or or_50 (or_50_out, and_74_out, in_2);
  or or_51 (or_51_out, and_48_out, in_1);
  D_Flip_Flop #(.trigger("falling")) d_ff_44 (.D(or_52_out), .clk(clock_1_out), .Q(out_16));  // open: Qn, preset, reset
  or or_52 (or_52_out, and_127_out, and_128_out);
  and and_128 (and_128_out, not_56_out, out_16);
  not not_56 (not_56_out, d_ff_1_q);
  or or_53 (or_53_out, and_93_out, or_54_out);
  or or_54 (or_54_out, and_94_out, or_55_out);
  or or_55 (or_55_out, and_95_out, or_56_out);
  or or_56 (or_56_out, and_96_out, or_57_out);
  or or_57 (or_57_out, and_97_out, or_58_out);
  or or_58 (or_58_out, and_98_out, or_59_out);
  or or_59 (or_59_out, and_99_out, or_60_out);
  or or_60 (or_60_out, and_100_out, in_3);
  or or_61 (or_61_out, and_119_out, or_62_out);
  or or_62 (or_62_out, and_120_out, or_63_out);
  or or_63 (or_63_out, and_121_out, or_64_out);
  or or_64 (or_64_out, and_122_out, or_65_out);
  or or_65 (or_65_out, and_123_out, or_66_out);
  or or_66 (or_66_out, and_124_out, or_67_out);
  or or_67 (or_67_out, and_125_out, or_68_out);
  or or_68 (or_68_out, and_126_out, in_4);

  // Notes on the sheet:
  //   circuit clock
  //   mode
  //   register
  //   Diana Covaci, 261086280
  //   msb on the left or on top (standard convention)
  //   address
  //   register
  //   input pins
  //   input register
  //   output pins
  //   bus
  //   register 7
  //   register 6
  //   register 2
  //   register 1
  //   register 0
  //   register 5
  //   register 4
  //   register 3
  //   output register
endmodule
